// Logisim project CPU.circ as structural Verilog
module main (
);

  RF rf_1 ();  // open: rd, load, rs1Addr, rdAddr, clk, rs2Addr, rs1, rs2
endmodule

module RF (
  input  [31:0] rd,
  input  load,
  input  [4:0] rs1Addr,
  input  [4:0] rdAddr,
  input  clk,
  input  [4:0] rs2Addr,
  output [31:0] rs1,
  output [31:0] rs2
);

  wire and_1_out, and_2_out, and_3_out, and_4_out, and_5_out, and_6_out, and_7_out, and_8_out, and_9_out,
       and_10_out, and_11_out, and_12_out, and_13_out, and_14_out, and_15_out, and_16_out, and_17_out,
       and_18_out, and_19_out, and_20_out, and_21_out, and_22_out, and_23_out, and_24_out, and_25_out,
       and_26_out, and_27_out, and_28_out, and_29_out, and_30_out, and_31_out, and_32_out, decoder_1_out0,
       decoder_1_out1, decoder_1_out2, decoder_1_out3, decoder_1_out4, decoder_1_out5, decoder_1_out6,
       decoder_1_out7, decoder_1_out8, decoder_1_out9, decoder_1_out10, decoder_1_out11, decoder_1_out12,
       decoder_1_out13, decoder_1_out14, decoder_1_out15, decoder_1_out16, decoder_1_out17, decoder_1_out18,
       decoder_1_out19, decoder_1_out20, decoder_1_out21, decoder_1_out22, decoder_1_out23, decoder_1_out24,
       decoder_1_out25, decoder_1_out26, decoder_1_out27, decoder_1_out28, decoder_1_out29, decoder_1_out30,
       decoder_1_out31;
  wire [31:0] register_1_q, register_2_q, register_3_q, register_4_q, register_5_q, register_6_q,
       register_7_q, register_8_q, register_9_q, register_10_q, register_11_q, register_12_q, register_13_q,
       register_14_q, register_15_q, register_16_q, register_17_q, register_18_q, register_19_q,
       register_20_q, register_21_q, register_22_q, register_23_q, register_24_q, register_25_q,
       register_26_q, register_27_q, register_28_q, undriven, undriven_2, x0_q, x1_q, x2_q, x3_q;

  Decoder #(.select(5)) decoder_1 (
    .out0(decoder_1_out0), .out1(decoder_1_out1), .out2(decoder_1_out2), .out3(decoder_1_out3),
    .out4(decoder_1_out4), .out5(decoder_1_out5), .out6(decoder_1_out6), .out7(decoder_1_out7),
    .out8(decoder_1_out8), .out9(decoder_1_out9), .out10(decoder_1_out10), .out11(decoder_1_out11),
    .out12(decoder_1_out12), .out13(decoder_1_out13), .out14(decoder_1_out14), .out15(decoder_1_out15),
    .out16(decoder_1_out16), .out17(decoder_1_out17), .out18(decoder_1_out18), .out19(decoder_1_out19),
    .out20(decoder_1_out20), .out21(decoder_1_out21), .out22(decoder_1_out22), .out23(decoder_1_out23),
    .out24(decoder_1_out24), .out25(decoder_1_out25), .out26(decoder_1_out26), .out27(decoder_1_out27),
    .out28(decoder_1_out28), .out29(decoder_1_out29), .out30(decoder_1_out30), .out31(decoder_1_out31),
    .sel(rdAddr));  // open: en
  and and_1 (and_1_out, load, decoder_1_out0);
  and and_2 (and_2_out, load, decoder_1_out1);
  and and_3 (and_3_out, load, decoder_1_out2);
  and and_4 (and_4_out, load, decoder_1_out3);
  Register #(.width(32)) x0 (.D(rd), .en(and_1_out), .clk(clk), .Q(x0_q));  // open: clr
  Register #(.width(32)) x1 (.D(rd), .en(and_2_out), .clk(clk), .Q(x1_q));  // open: clr
  Register #(.width(32)) x2 (.D(rd), .en(and_3_out), .clk(clk), .Q(x2_q));  // open: clr
  Register #(.width(32)) x3 (.D(rd), .en(and_4_out), .clk(clk), .Q(x3_q));  // open: clr
  Register #(.width(32)) register_1 (.D(rd), .en(and_5_out), .clk(clk), .Q(register_1_q));  // open: clr
  and and_5 (and_5_out, load, decoder_1_out16);
  Register #(.width(32)) register_2 (.D(rd), .en(and_6_out), .clk(clk), .Q(register_2_q), .clr(decoder_1_out24));
  and and_6 (and_6_out, load, decoder_1_out17);
  Register #(.width(32)) register_3 (.D(rd), .en(and_7_out), .clk(clk), .Q(register_3_q), .clr(decoder_1_out28));
  and and_7 (and_7_out, load, decoder_1_out18);
  Register #(.width(32)) register_4 (.D(rd), .en(and_8_out), .clk(clk), .Q(register_4_q));  // open: clr
  and and_8 (and_8_out, load, decoder_1_out19);
  and and_9 (and_9_out, and_1_out, decoder_1_out4);
  and and_10 (and_10_out, and_1_out, decoder_1_out5);
  and and_11 (and_11_out, and_1_out, decoder_1_out6);
  and and_12 (and_12_out, and_1_out, decoder_1_out7);
  and and_13 (and_13_out, load, decoder_1_out20);
  and and_14 (and_14_out, load, decoder_1_out21);
  and and_15 (and_15_out, load, decoder_1_out22);
  and and_16 (and_16_out, load, decoder_1_out23);
  Register #(.width(32)) register_5 (.D(rd), .en(and_9_out), .clk(clk), .Q(register_5_q));  // open: clr
  Register #(.width(32)) register_6 (.D(rd), .en(and_10_out), .clk(clk), .Q(register_6_q));  // open: clr
  Register #(.width(32)) register_7 (.D(rd), .en(and_11_out), .clk(clk), .Q(register_7_q));  // open: clr
  Register #(.width(32)) register_8 (.D(rd), .en(and_12_out), .clk(clk), .Q(register_8_q));  // open: clr
  Register #(.width(32)) register_9 (.D(rd), .en(and_13_out), .clk(clk), .Q(register_9_q));  // open: clr
  Register #(.width(32)) register_10 (.D(rd), .en(and_14_out), .clk(clk), .Q(register_10_q), .clr(decoder_1_out24));
  Register #(.width(32)) register_11 (.D(rd), .en(and_15_out), .clk(clk), .Q(register_11_q), .clr(decoder_1_out28));
  Register #(.width(32)) register_12 (.D(rd), .en(and_16_out), .clk(clk), .Q(register_12_q));  // open: clr
  Register #(.width(32)) register_13 (.D(undriven), .en(and_17_out), .clk(clk), .Q(register_13_q));  // open: clr
  and and_17 (and_17_out, and_1_out, decoder_1_out8);
  Register #(.width(32)) register_14 (.D(undriven), .en(and_18_out), .clk(clk), .Q(register_14_q));  // open: clr
  and and_18 (and_18_out, and_1_out, decoder_1_out9);
  Register #(.width(32)) register_15 (.D(undriven), .en(and_19_out), .clk(clk), .Q(register_15_q));  // open: clr
  and and_19 (and_19_out, and_1_out, decoder_1_out10);
  Register #(.width(32)) register_16 (.D(undriven), .en(and_20_out), .clk(clk), .Q(register_16_q));  // open: clr
  and and_20 (and_20_out, and_1_out, decoder_1_out11);
  Register #(.width(32)) register_17 (.D(undriven_2), .en(and_21_out), .clk(clk), .Q(register_17_q));  // open: clr
  and and_21 (and_21_out, load, decoder_1_out24);
  Register #(.width(32)) register_18 (.D(undriven_2), .en(and_22_out), .clk(clk), .Q(register_18_q));  // open: clr
  and and_22 (and_22_out, load, decoder_1_out25);
  Register #(.width(32)) register_19 (
    .D(undriven_2), .en(and_23_out), .clk(clk), .Q(register_19_q), .clr(decoder_1_out28));
  and and_23 (and_23_out, load, decoder_1_out26);
  Register #(.width(32)) register_20 (.D(undriven_2), .en(and_24_out), .clk(clk), .Q(register_20_q));  // open: clr
  and and_24 (and_24_out, load, decoder_1_out27);
  Register #(.width(32)) register_21 (.D(rd), .en(and_25_out), .clk(clk), .Q(register_21_q));  // open: clr
  and and_25 (and_25_out, and_1_out, decoder_1_out12);
  Register #(.width(32)) register_22 (.D(rd), .en(and_26_out), .clk(clk), .Q(register_22_q));  // open: clr
  and and_26 (and_26_out, and_1_out, decoder_1_out13);
  Register #(.width(32)) register_23 (.D(rd), .en(and_27_out), .clk(clk), .Q(register_23_q));  // open: clr
  and and_27 (and_27_out, and_1_out, decoder_1_out14);
  Register #(.width(32)) register_24 (.D(rd), .en(and_28_out), .clk(clk), .Q(register_24_q));  // open: clr
  and and_28 (and_28_out, and_1_out, decoder_1_out15);
  Register #(.width(32)) register_25 (.D(rd), .en(and_29_out), .clk(clk), .Q(register_25_q));  // open: clr
  and and_29 (and_29_out, load, decoder_1_out28);
  Register #(.width(32)) register_26 (.D(rd), .en(and_30_out), .clk(clk), .Q(register_26_q));  // open: clr
  and and_30 (and_30_out, load, decoder_1_out29);
  Register #(.width(32)) register_27 (.D(rd), .en(and_31_out), .clk(clk), .Q(register_27_q));  // open: clr
  and and_31 (and_31_out, load, decoder_1_out30);
  Register #(.width(32)) register_28 (.D(rd), .en(and_32_out), .clk(clk), .Q(register_28_q));  // open: clr
  and and_32 (and_32_out, load, decoder_1_out31);
  Multiplexer #(.select(5), .width(32)) multiplexer_1 (
    .in0(x0_q), .in1(x1_q), .in2(x2_q), .in3(x3_q), .in4(register_5_q), .in5(register_6_q),
    .in6(register_7_q), .in7(register_8_q), .in8(register_13_q), .in9(register_14_q), .in10(register_15_q),
    .in11(register_16_q), .in12(register_21_q), .in13(register_22_q), .in14(register_23_q),
    .in15(register_24_q), .in16(register_1_q), .in17(register_2_q), .in18(register_3_q), .in19(register_4_q),
    .in20(register_9_q), .in21(register_10_q), .in22(register_11_q), .in23(register_12_q),
    .in24(register_17_q), .in25(register_18_q), .in26(register_19_q), .in27(register_20_q),
    .in28(register_25_q), .in29(register_26_q), .in30(register_27_q), .in31(register_28_q), .out(rs1),
    .sel(rs1Addr));
  Multiplexer #(.select(5), .width(32)) multiplexer_2 (
    .in0(x0_q), .in1(x1_q), .in2(x2_q), .in3(x3_q), .in4(register_5_q), .in5(register_6_q),
    .in6(register_7_q), .in7(register_8_q), .in8(register_13_q), .in9(register_14_q), .in10(register_15_q),
    .in11(register_16_q), .in12(register_21_q), .in13(register_22_q), .in14(register_23_q),
    .in15(register_24_q), .in16(register_1_q), .in17(register_2_q), .in18(register_3_q), .in19(register_4_q),
    .in20(register_9_q), .in21(register_10_q), .in22(register_11_q), .in23(register_12_q),
    .in24(register_17_q), .in25(register_18_q), .in26(register_19_q), .in27(register_20_q),
    .in28(register_25_q), .in29(register_26_q), .in30(register_27_q), .in31(register_28_q), .out(rs2),
    .sel(rs2Addr));
endmodule
